# Fritzing sketch schematics (saved by Fritzing 0.9.0b)

parts:
  Magnetic_reed_switch = SWITCH-MOMENTARY-2 [package=reed_switch_pth]
  R1 = Resistor [tolerance=±5% resistance=10k package=THT]
  Part2 = Arduino Nano (Rev3.0)

nets:
  N1: Magnetic_reed_switch.1, Part2.A0
  N2: Magnetic_reed_switch.2, R1.Pin_0
  N3: R1.Pin_1, Part2.GND

notes:
  Magnetic reed switch
  10 kΩ Resistor
